# Fritzing sketch pro mini (saved by Fritzing 0.9.2b)
breadboards: 2

parts:
  Part1 = Arduino Pro Mini v13
  LCD1 = LCD screen
  R1 = Resistor [tolerance=±5% resistance=220 package=THT]
  R2 = Trimmer Potentiometer [maximum_resistance=10kΩ package=THT]
  RHT1 = Humidity and Temperature Sensor RHT03
  K1 = Relay [part_number=FRS1B-S package=THT]
  Q1 = NPN-Transistor [part_number=BC548 package="TO92 [THT]"]
  D1 = Rectifier Diode [part_number=1N4001 package="300 mil [THT]"]
  R3 = Resistor [tolerance=±5% resistance=1k package=THT]
  VCC1 = 4 x AAA Battery Mount
  J2 = Screw terminal - 2 pins [package=THT]
  Tiny_RTC1 = Tiny RTC
  S1 = Pushbutton [package="[THT]"]
  S2 = Pushbutton [package="[THT]"]
  S3 = Pushbutton [package="[THT]"]
  S4 = Pushbutton [package="[THT]"]
  R4 = Resistor [tolerance=±5% resistance=10k package=THT]
  R5 = Resistor [tolerance=±5% resistance=10k package=THT]
  R6 = Resistor [tolerance=±5% resistance=10k package=THT]
  R7 = Resistor [tolerance=±5% resistance=10k package=THT]

nets:
  GND: Part1.GND, LCD1.VSS, LCD1.R/W, LCD1.LED-, R2.leg2, RHT1.GND_2, Q1.E, VCC1.-, Tiny_RTC1.GND, R4.Pin_1, R5.Pin_1, R6.Pin_1, R7.Pin_1
  N1: Part1.A4, Tiny_RTC1.SDA
  N2: Part1.A5, Tiny_RTC1.SCL
  N3: Part1.RAW, VCC1.+
  VCC: Part1.VCC, LCD1.VDD, R2.leg1, RHT1.Vcc, K1.COIL2, D1.cathode, Tiny_RTC1.VCC, S1.Pin_3, S1.Pin_4, S2.Pin_3, S2.Pin_4, S3.Pin_3, S3.Pin_4, S4.Pin_3, S4.Pin_4
  N4: Part1.A1, S2.Pin_1, S2.Pin_2, R7.Pin_0
  N5: Part1.A0, S4.Pin_1, S4.Pin_2, R5.Pin_0
  N6: Part1.D13/SCK, S3.Pin_1, S3.Pin_2, R6.Pin_0
  N7: Part1.D12/MISO, LCD1.RS
  N8: Part1.D11_PWM/MOSI, LCD1.E
  N9: Part1.D10_PWM/SS, R3.Pin_1
  N10: Part1.D9_PWM, R1.Pin_0
  N11: Part1.D7, S1.Pin_1, S1.Pin_2, R4.Pin_0
  N12: Part1.D6_PWM, RHT1.Data-signal
  N13: Part1.D5_PWM, LCD1.DB4
  N14: Part1.D4, LCD1.DB5
  N15: Part1.D3_PWM, LCD1.DB6
  N16: Part1.D2, LCD1.DB7
  N17: LCD1.V0, R2.wiper
  N18: LCD1.LED+, R1.Pin_1
  N19: K1.COIL1, Q1.C, D1.anode
  N20: K1.C2, J2.pin2
  N21: K1.B, J2.pin1
  N22: Q1.B, R3.Pin_0

custom parts:
  Tiny RTC: Tiny RTC I2C module DS1370Z RTC and AT24C32 EEPROM
